// Logisim project somador 32bit.circ as structural Verilog: 3 circuits, main circuit main
module main (
  input  A,
  input  B,
  input  Cin,
  output C_out,
  output S
);

  wire and_1_out, and_2_out, and_3_out, xor_1_out;

  and and_1 (and_1_out, A, A);
  and and_2 (and_2_out, A, Cin);
  and and_3 (and_3_out, B, Cin);
  xor xor_1 (xor_1_out, Cin, B);
  or or_1 (C_out, and_1_out, and_2_out, and_3_out);
  xor xor_2 (S, xor_1_out, A);
endmodule

module teste (
  input  [7:0] A,
  input  [7:0] B,
  input  C_in,
  output C_out,
  output [7:0] S
);

  wire main_2_c_out, main_3_c_out, main_4_c_out, main_5_c_out, main_6_c_out, main_7_c_out, main_8_c_out;

  main main_1 (.C_out(C_out), .S(S[7]), .A(A[7]), .B(B[7]), .Cin(main_2_c_out));
  main main_2 (.C_out(main_2_c_out), .S(S[6]), .A(A[6]), .B(B[6]), .Cin(main_3_c_out));
  main main_3 (.C_out(main_3_c_out), .S(S[5]), .A(A[5]), .B(B[5]), .Cin(main_4_c_out));
  main main_4 (.C_out(main_4_c_out), .S(S[4]), .A(A[4]), .B(B[4]), .Cin(main_5_c_out));
  main main_5 (.C_out(main_5_c_out), .S(S[3]), .A(A[3]), .B(B[3]), .Cin(main_6_c_out));
  main main_6 (.C_out(main_6_c_out), .S(S[2]), .A(A[2]), .B(B[2]), .Cin(main_7_c_out));
  main main_7 (.C_out(main_7_c_out), .S(S[1]), .A(A[1]), .B(B[1]), .Cin(main_8_c_out));
  main main_8 (.C_out(main_8_c_out), .S(S[0]), .A(A[0]), .B(B[0]), .Cin(C_in));
endmodule

module somador_32_bits (
  input  [31:0] A,
  input  [31:0] B,
  input  C_in,
  output C_out,
  output [31:0] out_5
);

  wire teste_2_c_out, teste_3_c_out, teste_4_c_out;

  teste teste_1 (.A(A[31:24]), .B(B[31:24]), .C_out(C_out), .S(out_5[31:24]), .C_in(teste_2_c_out));
  teste teste_2 (.A(A[23:16]), .B(B[23:16]), .C_out(teste_2_c_out), .S(out_5[23:16]), .C_in(teste_3_c_out));
  teste teste_3 (.A(A[15:8]), .B(B[15:8]), .C_out(teste_3_c_out), .S(out_5[15:8]), .C_in(teste_4_c_out));
  teste teste_4 (.A(A[7:0]), .B(B[7:0]), .C_out(teste_4_c_out), .S(out_5[7:0]), .C_in(C_in));
endmodule
