// Logisim project somador-subtrator.circ as structural Verilog: 2 circuits, main circuit main
module main (
  input  A,
  input  B,
  input  Cin,
  output S
);

  wire xor_1_out;

  xor xor_1 (xor_1_out, B, A);
  xor xor_2 (S, xor_1_out, Cin);
endmodule

module somador_subtrator_8bits (
  input  [7:0] A,
  input  [7:0] B,
  input  Op,
  output [7:0] S,
  output out_5
);

  wire and_1_out, and_2_out, and_3_out, and_4_out, and_5_out, and_6_out, and_7_out, and_8_out, and_9_out,
       and_10_out, and_11_out, and_12_out, and_13_out, and_14_out, and_15_out, and_16_out, and_17_out,
       and_18_out, and_19_out, and_20_out, and_21_out, and_22_out, and_23_out, and_24_out, and_25_out,
       and_26_out, and_27_out, and_28_out, and_29_out, and_30_out, and_31_out, and_32_out, and_33_out,
       and_34_out, and_35_out, and_36_out, G7_out, or_1_out, or_3_out, or_4_out, or_5_out, or_6_out,
       or_7_out, or_8_out, or_9_out, P0_out, P1_out, P2_out, P3_out, P4_out, P5_out, P6_out, P7_out;
  wire [6:0] G0_out;
  wire [7:0] xor_1_out;

  and and_1 (and_1_out, Op, Op, P0_out, P1_out, P2_out, P4_out, P5_out, P6_out, P7_out);
  and and_2 (and_2_out, G0_out[0], P0_out, P1_out, P2_out, P4_out, P5_out, P6_out, P7_out);
  and and_3 (and_3_out, G0_out[1], P1_out, P2_out, P4_out, P5_out, P6_out, P7_out);
  and and_4 (and_4_out, G0_out[2], P2_out, P4_out, P5_out, P6_out, P7_out);
  and and_5 (and_5_out, G0_out[3], P2_out, P4_out, P6_out, P7_out);
  and and_6 (and_6_out, G0_out[4], P4_out, P5_out, P7_out);
  and and_7 (and_7_out, G0_out[5], P6_out, P7_out);
  and and_8 (and_8_out, G0_out[6], P7_out);
  or or_1 (or_1_out, and_1_out, and_2_out, and_3_out, and_4_out, and_5_out, and_6_out, and_7_out, and_8_out);
  or or_2 (out_5, or_1_out, G7_out);
  assign xor_1_out = B ^ {8{Op}};  // XOR_Gate xor_1, 8 bits wide
  or P7 (P7_out, xor_1_out[7], xor_1_out[7]);
  and G7 (G7_out, xor_1_out[7], xor_1_out[7]);
  and and_9 (and_9_out, Op, P0_out, P1_out, P2_out, P3_out, P4_out, P5_out, P6_out);
  main main_1 (.S(S[7]), .A(xor_1_out[7]), .B(A[7]), .Cin(or_3_out));
  and and_10 (and_10_out, P6_out, P5_out, P4_out, P3_out, P2_out, P1_out, G0_out[0]);
  or or_3 (or_3_out, and_9_out, and_10_out, and_11_out, and_12_out, and_14_out, and_13_out, and_15_out, G0_out[6]);
  and and_11 (and_11_out, P6_out, P5_out, P4_out, P3_out, P2_out, G0_out[1]);
  and and_12 (and_12_out, P6_out, P5_out, P4_out, P3_out, G0_out[2]);
  and and_13 (and_13_out, P6_out, P5_out, G0_out[4]);
  and and_14 (and_14_out, P6_out, P5_out, P4_out, G0_out[3]);
  and and_15 (and_15_out, P6_out, G0_out[5]);
  or P6 (P6_out, xor_1_out[6], A[6]);
  and G6 (G0_out[6], xor_1_out[6], A[6]);
  and and_16 (and_16_out, Op, P0_out, P1_out, P2_out, P3_out, P4_out, P5_out);
  main main_2 (.S(S[6]), .A(A[6]), .B(xor_1_out[6]), .Cin(or_4_out));
  and and_17 (and_17_out, P5_out, P4_out, P3_out, P2_out, P1_out, G0_out[0]);
  or or_4 (or_4_out, and_16_out, and_17_out, and_18_out, and_19_out, and_20_out, and_21_out, G0_out[5]);
  and and_18 (and_18_out, P5_out, P4_out, P3_out, P2_out, G0_out[1]);
  and and_19 (and_19_out, P5_out, P4_out, P3_out, G0_out[2]);
  and and_20 (and_20_out, P4_out, P5_out, G0_out[3]);
  or P5 (P5_out, xor_1_out[5], A[5]);
  and G5 (G0_out[5], xor_1_out[5], A[5]);
  and and_21 (and_21_out, P5_out, G0_out[4]);
  and and_22 (and_22_out, Op, P0_out, P1_out, P2_out, P3_out, P4_out);
  or or_5 (or_5_out, and_22_out, and_23_out, and_24_out, and_25_out, and_26_out, G0_out[4]);
  main main_3 (.S(S[5]), .A(A[5]), .B(xor_1_out[5]), .Cin(or_5_out));
  and and_23 (and_23_out, P4_out, P3_out, P2_out, P1_out, G0_out[0]);
  and and_24 (and_24_out, P4_out, P3_out, P2_out, G0_out[1]);
  and and_25 (and_25_out, P4_out, P3_out, G0_out[2]);
  or P4 (P4_out, xor_1_out[4], A[4]);
  and G4 (G0_out[4], xor_1_out[4], A[4]);
  and and_26 (and_26_out, P4_out, G0_out[3]);
  and and_27 (and_27_out, Op, P0_out, P1_out, P2_out, P3_out);
  main main_4 (.S(S[4]), .A(A[4]), .B(xor_1_out[4]), .Cin(or_6_out));
  and and_28 (and_28_out, P3_out, P2_out, P1_out, G0_out[0]);
  or or_6 (or_6_out, and_27_out, and_28_out, and_30_out, and_29_out, G0_out[3]);
  or P3 (P3_out, xor_1_out[3], A[3]);
  and G3 (G0_out[3], xor_1_out[3], A[3]);
  and and_29 (and_29_out, P3_out, G0_out[2]);
  and and_30 (and_30_out, P3_out, P2_out, G0_out[1]);
  and and_31 (and_31_out, P2_out, P1_out, G0_out[0]);
  and and_32 (and_32_out, Op, P0_out, P1_out, P2_out);
  or or_7 (or_7_out, and_32_out, and_31_out, and_33_out, G0_out[2]);
  main main_5 (.S(S[3]), .A(A[3]), .B(xor_1_out[3]), .Cin(or_7_out));
  or P2 (P2_out, xor_1_out[2], A[2]);
  and G2 (G0_out[2], xor_1_out[2], A[2]);
  and and_33 (and_33_out, P2_out, G0_out[1]);
  and and_34 (and_34_out, P0_out, P1_out, Op);
  or or_8 (or_8_out, and_34_out, and_35_out, G0_out[1]);
  main main_6 (.S(S[2]), .A(A[2]), .B(xor_1_out[2]), .Cin(or_8_out));
  or P1 (P1_out, xor_1_out[1], A[1]);
  and G1 (G0_out[1], xor_1_out[1], A[1]);
  and and_35 (and_35_out, P1_out, G0_out[0]);
  main main_7 (.S(S[1]), .A(A[1]), .B(xor_1_out[1]), .Cin(or_9_out));
  or P0 (P0_out, xor_1_out[0], A[0]);
  and G0 (G0_out[0], xor_1_out[0], A[0]);
  and and_36 (and_36_out, P0_out, Op);
  or or_9 (or_9_out, and_36_out, G0_out[0]);
  main main_8 (.S(S[0]), .A(A[0]), .B(xor_1_out[0]), .Cin(Op));
endmodule
