// Logisim project contador.circ as structural Verilog: 4 circuits, main circuit Min/Sec
module Min_Sec (
  input  Clock,
  output [3:0] Seg,
  output [3:0] Seg_2,
  output [3:0] DecSeg,
  output Contador
);

  wire and_1_out, clock_1_out, undriven;

  and and_1 (and_1_out, DecSeg[3], ~DecSeg[2], DecSeg[1], ~DecSeg[0]);  // AND_Gate
  and and_2 (Contador, Seg_2[2], Seg_2[1], ~Seg_2[0]);  // AND_Gate
  T_Flip_Flop #(.trigger("falling")) t_ff_1 (
    .clk(Clock), .T(1'b1), .Q(DecSeg[0]), .reset(and_1_out));  // open: Qn, preset, en
  T_Flip_Flop #(.trigger("falling")) t_ff_2 (
    .clk(and_1_out), .T(1'b1), .Q(Seg_2[0]), .reset(Contador));  // open: Qn, preset, en
  T_Flip_Flop #(.trigger("falling")) t_ff_3 (
    .clk(DecSeg[0]), .T(1'b1), .Q(DecSeg[1]), .reset(and_1_out));  // open: Qn, preset, en
  T_Flip_Flop #(.trigger("falling")) t_ff_4 (
    .clk(Seg_2[0]), .T(1'b1), .Q(Seg_2[1]), .reset(Contador));  // open: Qn, preset, en
  T_Flip_Flop #(.trigger("falling")) t_ff_5 (
    .clk(DecSeg[1]), .T(1'b1), .Q(DecSeg[2]), .reset(and_1_out));  // open: Qn, preset, en
  T_Flip_Flop #(.trigger("falling")) t_ff_6 (
    .clk(Seg_2[1]), .T(1'b1), .Q(Seg_2[2]), .reset(Contador));  // open: Qn, preset, en
  Hex_Digit_Display hex_digit_display_1 (.value(DecSeg));  // open: dp
  Hex_Digit_Display hex_digit_display_2 (.value({1'b0, Seg_2[2:0]}));  // open: dp
  T_Flip_Flop #(.trigger("falling")) t_ff_7 (
    .clk(DecSeg[2]), .T(1'b1), .Q(DecSeg[3]), .reset(and_1_out));  // open: Qn, preset, en
  Clock clock_1 (.out(clock_1_out));
  // AND_Gate and_3 has open pins: in0=Seg[0], in1=Seg[1], in2=Seg[2], out=open
  T_Flip_Flop #(.trigger("falling")) t_ff_8 (
    .clk(Seg[1]), .T(1'b1), .Q(Seg[2]), .preset(undriven));  // open: Qn, reset, en
  T_Flip_Flop #(.trigger("falling")) t_ff_9 (
    .clk(Seg[0]), .T(1'b1), .Q(Seg[1]), .preset(undriven));  // open: Qn, reset, en
  Hex_Digit_Display hex_digit_display_3 (.value({1'b0, Seg[2:0]}));  // open: dp
  T_Flip_Flop #(.trigger("falling")) t_ff_10 (
    .clk(clock_1_out), .T(1'b1), .Q(Seg[0]), .preset(undriven));  // open: Qn, reset, en

  assign Seg[3] = 1'b0;
  assign Seg_2[3] = 1'b0;
endmodule

module Main (
);

  wire clock_1_out, min_sec_1_contador, min_sec_2_contador;
  wire [3:0] CMili, DecHr, DecMin, DecSec, DMili, Hr, Min, MMili, Sec;

  Hex_Digit_Display hex_digit_display_1 (.value(DecHr));  // open: dp
  Hex_Digit_Display hex_digit_display_2 (.value(Hr));  // open: dp
  Clock #(.highDuration(2), .lowDuration(2)) clock_1 (.out(clock_1_out));
  Mili mili_1 (.MiliMili(MMili), .CentMili(CMili), .DecMili(DMili));  // open: Clock, Contador
  Hex_Digit_Display hex_digit_display_3 (.value(DecMin));  // open: dp
  Hex_Digit_Display hex_digit_display_4 (.value(Min));  // open: dp
  Min_Sec min_sec_1 (.Clock(clock_1_out), .Seg_2(DecSec), .DecSeg(Sec), .Contador(min_sec_1_contador));  // open: Seg
  Hex_Digit_Display hex_digit_display_5 (.value(DecSec));  // open: dp
  Min_Sec min_sec_2 (
    .Clock(min_sec_1_contador), .Seg_2(DecMin), .DecSeg(Min), .Contador(min_sec_2_contador));  // open: Seg
  Hex_Digit_Display hex_digit_display_6 (.value(Sec));  // open: dp
  Horas horas_1 (.Clock(min_sec_2_contador), .Seg(DecHr), .DecSeg(Hr));  // open: Contador
  Hex_Digit_Display hex_digit_display_7 (.value(DMili));  // open: dp
  Hex_Digit_Display hex_digit_display_8 (.value(MMili));  // open: dp
  Hex_Digit_Display hex_digit_display_9 (.value(CMili));  // open: dp
endmodule

module Horas (
  input  Clock,
  output [3:0] Seg,
  output [3:0] DecSeg,
  output Contador
);

  wire and_1_out, and_2_out, and_3_out, multiplexer_1_out;

  and and_1 (and_1_out, ~DecSeg[3], DecSeg[2], ~DecSeg[1], ~DecSeg[0]);  // AND_Gate
  Multiplexer #(.enable("false")) multiplexer_1 (
    .in0(and_3_out), .in1(and_1_out), .out(multiplexer_1_out), .sel(and_2_out));
  and and_2 (and_2_out, ~Seg[0], Seg[1]);  // AND_Gate
  and and_3 (and_3_out, DecSeg[3], ~DecSeg[2], DecSeg[1], ~DecSeg[0]);  // AND_Gate
  and and_4 (Contador, Seg[1], Seg[0]);
  T_Flip_Flop #(.trigger("falling")) t_ff_1 (
    .clk(Clock), .T(1'b1), .Q(DecSeg[0]), .reset(multiplexer_1_out));  // open: Qn, preset, en
  T_Flip_Flop #(.trigger("falling")) t_ff_2 (
    .clk(multiplexer_1_out), .T(1'b1), .Q(Seg[0]), .reset(Contador));  // open: Qn, preset, en
  T_Flip_Flop #(.trigger("falling")) t_ff_3 (
    .clk(DecSeg[0]), .T(1'b1), .Q(DecSeg[1]), .reset(multiplexer_1_out));  // open: Qn, preset, en
  T_Flip_Flop #(.trigger("falling")) t_ff_4 (
    .clk(Seg[0]), .T(1'b1), .Q(Seg[1]), .reset(Contador));  // open: Qn, preset, en
  T_Flip_Flop #(.trigger("falling")) t_ff_5 (
    .clk(DecSeg[1]), .T(1'b1), .Q(DecSeg[2]), .reset(multiplexer_1_out));  // open: Qn, preset, en
  Hex_Digit_Display hex_digit_display_1 (.value(DecSeg));  // open: dp
  Hex_Digit_Display hex_digit_display_2 (.value({2'b00, Seg[1:0]}));  // open: dp
  T_Flip_Flop #(.trigger("falling")) t_ff_6 (
    .clk(DecSeg[2]), .T(1'b1), .Q(DecSeg[3]), .reset(multiplexer_1_out));  // open: Qn, preset, en

  assign Seg[3:2] = 2'b00;
endmodule

module Mili (
  input  Clock,
  output [3:0] MiliMili,
  output [3:0] CentMili,
  output [3:0] DecMili,
  output Contador
);

  wire and_1_out, and_2_out;

  and and_1 (and_1_out, MiliMili[3], ~MiliMili[2], MiliMili[1], ~MiliMili[0]);  // AND_Gate
  and and_2 (and_2_out, CentMili[3], ~CentMili[2], CentMili[1], ~CentMili[0]);  // AND_Gate
  and and_3 (Contador, DecMili[3], ~DecMili[2], DecMili[1], ~DecMili[0]);  // AND_Gate
  T_Flip_Flop #(.trigger("falling")) t_ff_1 (
    .clk(Clock), .T(1'b1), .Q(MiliMili[0]), .reset(and_1_out));  // open: Qn, preset, en
  T_Flip_Flop #(.trigger("falling")) t_ff_2 (
    .clk(and_1_out), .T(1'b1), .Q(CentMili[0]), .reset(and_2_out));  // open: Qn, preset, en
  T_Flip_Flop #(.trigger("falling")) t_ff_3 (
    .clk(and_2_out), .T(1'b1), .Q(DecMili[0]), .reset(Contador));  // open: Qn, preset, en
  T_Flip_Flop #(.trigger("falling")) t_ff_4 (
    .clk(MiliMili[0]), .T(1'b1), .Q(MiliMili[1]), .reset(and_1_out));  // open: Qn, preset, en
  T_Flip_Flop #(.trigger("falling")) t_ff_5 (
    .clk(CentMili[0]), .T(1'b1), .Q(CentMili[1]), .reset(and_2_out));  // open: Qn, preset, en
  T_Flip_Flop #(.trigger("falling")) t_ff_6 (
    .clk(DecMili[0]), .T(1'b1), .Q(DecMili[1]), .reset(Contador));  // open: Qn, preset, en
  T_Flip_Flop #(.trigger("falling")) t_ff_7 (
    .clk(MiliMili[1]), .T(1'b1), .Q(MiliMili[2]), .reset(and_1_out));  // open: Qn, preset, en
  T_Flip_Flop #(.trigger("falling")) t_ff_8 (
    .clk(CentMili[1]), .T(1'b1), .Q(CentMili[2]), .reset(and_2_out));  // open: Qn, preset, en
  T_Flip_Flop #(.trigger("falling")) t_ff_9 (
    .clk(DecMili[1]), .T(1'b1), .Q(DecMili[2]), .reset(Contador));  // open: Qn, preset, en
  T_Flip_Flop #(.trigger("falling")) t_ff_10 (
    .clk(MiliMili[2]), .T(1'b1), .Q(MiliMili[3]), .reset(and_1_out));  // open: Qn, preset, en
  T_Flip_Flop #(.trigger("falling")) t_ff_11 (
    .clk(CentMili[2]), .T(1'b1), .Q(CentMili[3]), .reset(and_2_out));  // open: Qn, preset, en
  T_Flip_Flop #(.trigger("falling")) t_ff_12 (
    .clk(DecMili[2]), .T(1'b1), .Q(DecMili[3]), .reset(Contador));  // open: Qn, preset, en
  Hex_Digit_Display hex_digit_display_1 (.value(DecMili));  // open: dp
  Hex_Digit_Display hex_digit_display_2 (.value(CentMili));  // open: dp
  Hex_Digit_Display hex_digit_display_3 (.value(MiliMili));  // open: dp
endmodule
