// Logisim project divisor.circ as structural Verilog: 3 circuits, main circuit main
module main (
  input  [7:0] Dividendo,
  input  [7:0] Divisor,
  output [7:0] Quociente,
  output [7:0] Resto
);

  wire subtrator_1_bit, subtrator_2_bit, subtrator_3_bit, subtrator_4_bit, subtrator_5_bit, subtrator_6_bit,
       subtrator_7_bit, subtrator_8_bit;
  wire [7:0] multiplexer_1_out, multiplexer_2_out, multiplexer_4_out, multiplexer_5_out, multiplexer_6_out,
       multiplexer_7_out, subtrator_1_s, subtrator_2_s, subtrator_3_s, subtrator_4_s, subtrator_5_s,
       subtrator_6_s, subtrator_7_s, subtrator_8_s;
  wire [7:1] multiplexer_3_out_2;
  wire [7:7] multiplexer_3_out;

  subtrator subtrator_1 (
    .A({{7{1'b0}}, Dividendo[7]}), .B(Divisor), .Op(1'b1), .S(subtrator_1_s), .Bit(subtrator_1_bit));  // open: Cout
  not not_1 (Quociente[7], subtrator_1_bit);
  Multiplexer #(.width(8), .enable("false")) multiplexer_1 (
    .in0(subtrator_1_s), .in1({{7{1'b0}}, Dividendo[7]}), .out(multiplexer_1_out), .sel(subtrator_1_bit));
  not not_2 (Quociente[6], subtrator_2_bit);
  subtrator subtrator_2 (
    .A({multiplexer_1_out[6:0], Dividendo[6]}), .B(Divisor), .Op(1'b1), .S(subtrator_2_s),
    .Bit(subtrator_2_bit));  // open: Cout
  Multiplexer #(.width(8), .enable("false")) multiplexer_2 (
    .in0(subtrator_2_s), .in1({multiplexer_1_out[6:0], Dividendo[6]}), .out(multiplexer_2_out),
    .sel(subtrator_2_bit));
  subtrator subtrator_3 (
    .A({multiplexer_2_out[6:0], Dividendo[5]}), .B(Divisor), .Op(1'b1), .S(subtrator_3_s),
    .Bit(subtrator_3_bit));  // open: Cout
  not not_3 (Quociente[5], subtrator_3_bit);
  Multiplexer #(.width(8), .enable("false")) multiplexer_3 (
    .in0(subtrator_3_s), .in1({multiplexer_2_out[6:0], Dividendo[5]}),
    .out({multiplexer_3_out[7], multiplexer_3_out_2}), .sel(subtrator_3_bit));
  subtrator subtrator_4 (
    .A({multiplexer_3_out_2, Dividendo[4]}), .B(Divisor), .Op(1'b1), .S(subtrator_4_s), .Bit(subtrator_4_bit));  // open: Cout
  not not_4 (Quociente[4], subtrator_4_bit);
  Multiplexer #(.width(8), .enable("false")) multiplexer_4 (
    .in0(subtrator_4_s), .in1({multiplexer_3_out_2, Dividendo[4]}), .out(multiplexer_4_out),
    .sel(subtrator_4_bit));
  subtrator subtrator_5 (
    .A({multiplexer_4_out[6:0], Dividendo[3]}), .B(Divisor), .Op(1'b1), .S(subtrator_5_s),
    .Bit(subtrator_5_bit));  // open: Cout
  not not_5 (Quociente[3], subtrator_5_bit);
  Multiplexer #(.width(8), .enable("false")) multiplexer_5 (
    .in0(subtrator_5_s), .in1({multiplexer_4_out[6:0], Dividendo[3]}), .out(multiplexer_5_out),
    .sel(subtrator_5_bit));
  not not_6 (Quociente[2], subtrator_6_bit);
  subtrator subtrator_6 (
    .A({multiplexer_5_out[6:0], Dividendo[2]}), .B(Divisor), .Op(1'b1), .S(subtrator_6_s),
    .Bit(subtrator_6_bit));  // open: Cout
  Multiplexer #(.width(8), .enable("false")) multiplexer_6 (
    .in0(subtrator_6_s), .in1({multiplexer_5_out[6:0], Dividendo[2]}), .out(multiplexer_6_out),
    .sel(subtrator_6_bit));
  not not_7 (Quociente[1], subtrator_7_bit);
  subtrator subtrator_7 (
    .A({multiplexer_6_out[6:0], Dividendo[1]}), .B(Divisor), .Op(1'b1), .S(subtrator_7_s),
    .Bit(subtrator_7_bit));  // open: Cout
  Multiplexer #(.width(8), .enable("false")) multiplexer_7 (
    .in0(subtrator_7_s), .in1({multiplexer_6_out[6:0], Dividendo[1]}), .out(multiplexer_7_out),
    .sel(subtrator_7_bit));
  subtrator subtrator_8 (
    .A({multiplexer_7_out[6:0], Dividendo[0]}), .B(Divisor), .Op(1'b1), .S(subtrator_8_s),
    .Bit(subtrator_8_bit));  // open: Cout
  not not_8 (Quociente[0], subtrator_8_bit);
  Multiplexer #(.width(8), .enable("false")) multiplexer_8 (
    .in0(subtrator_8_s), .in1({multiplexer_7_out[6:0], Dividendo[0]}), .out(Resto), .sel(subtrator_8_bit));

  // Other names for the same wires on the sheet: D[7:0] = Dividendo; Div[7:0] = Divisor; S7 = Quociente[0];
  //   S6 = Quociente[1]; S5 = Quociente[2]; S4 = Quociente[3]; S3 = Quociente[4]; S2 = Quociente[5];
  //   S1 = Quociente[6]; S0 = Quociente[7]
endmodule

module subtrator (
  input  [7:0] A,
  input  [7:0] B,
  input  Op,
  output [7:0] S,
  output Bit,
  output Cout
);

  wire and_1_out, and_2_out, and_3_out, and_4_out, and_5_out, and_6_out, and_7_out, and_8_out, and_9_out,
       and_10_out, and_11_out, and_12_out, and_13_out, and_14_out, and_15_out, and_16_out, and_17_out,
       and_18_out, and_19_out, and_20_out, and_21_out, and_22_out, and_23_out, and_24_out, and_25_out,
       and_26_out, and_27_out, and_28_out, and_29_out, and_30_out, and_31_out, and_32_out, and_33_out,
       and_34_out, and_35_out, and_36_out, G7_out, or_1_out, or_3_out, or_4_out, or_5_out, or_6_out,
       or_7_out, or_8_out, or_9_out, P0_out, P1_out, P2_out, P3_out, P4_out, P5_out, P6_out, P7_out;
  wire [6:0] G0_out;
  wire [7:0] xor_1_out;

  and and_1 (and_1_out, Op, Op, P0_out, P1_out, P2_out, P4_out, P5_out, P6_out, P7_out);
  and and_2 (and_2_out, G0_out[0], P0_out, P1_out, P2_out, P4_out, P5_out, P6_out, P7_out);
  and and_3 (and_3_out, G0_out[1], P1_out, P2_out, P4_out, P5_out, P6_out, P7_out);
  and and_4 (and_4_out, G0_out[2], P2_out, P4_out, P5_out, P6_out, P7_out);
  and and_5 (and_5_out, G0_out[3], P2_out, P4_out, P6_out, P7_out);
  and and_6 (and_6_out, G0_out[4], P4_out, P5_out, P7_out);
  and and_7 (and_7_out, G0_out[5], P6_out, P7_out);
  and and_8 (and_8_out, G0_out[6], P7_out);
  or or_1 (or_1_out, and_1_out, and_2_out, and_3_out, and_4_out, and_5_out, and_6_out, and_7_out, and_8_out);
  or or_2 (Cout, or_1_out, G7_out);
  assign xor_1_out = B ^ {8{Op}};  // XOR_Gate xor_1, 8 bits wide
  or P7 (P7_out, xor_1_out[7], xor_1_out[7]);
  and G7 (G7_out, xor_1_out[7], xor_1_out[7]);
  and and_9 (and_9_out, Op, P0_out, P1_out, P2_out, P3_out, P4_out, P5_out, P6_out);
  and and_10 (and_10_out, P6_out, P5_out, P4_out, P3_out, P2_out, P1_out, G0_out[0]);
  or or_3 (or_3_out, and_9_out, and_10_out, and_11_out, and_12_out, and_14_out, and_13_out, and_15_out, G0_out[6]);
  main_2 main_2_1 (.S(Bit), .A(xor_1_out[7]), .B(A[7]), .Cin(or_3_out));
  and and_11 (and_11_out, P6_out, P5_out, P4_out, P3_out, P2_out, G0_out[1]);
  and and_12 (and_12_out, P6_out, P5_out, P4_out, P3_out, G0_out[2]);
  and and_13 (and_13_out, P6_out, P5_out, G0_out[4]);
  and and_14 (and_14_out, P6_out, P5_out, P4_out, G0_out[3]);
  and and_15 (and_15_out, P6_out, G0_out[5]);
  or P6 (P6_out, xor_1_out[6], A[6]);
  and G6 (G0_out[6], xor_1_out[6], A[6]);
  and and_16 (and_16_out, Op, P0_out, P1_out, P2_out, P3_out, P4_out, P5_out);
  and and_17 (and_17_out, P5_out, P4_out, P3_out, P2_out, P1_out, G0_out[0]);
  or or_4 (or_4_out, and_16_out, and_17_out, and_18_out, and_19_out, and_20_out, and_21_out, G0_out[5]);
  main_2 main_2_2 (.S(S[6]), .A(A[6]), .B(xor_1_out[6]), .Cin(or_4_out));
  and and_18 (and_18_out, P5_out, P4_out, P3_out, P2_out, G0_out[1]);
  and and_19 (and_19_out, P5_out, P4_out, P3_out, G0_out[2]);
  and and_20 (and_20_out, P4_out, P5_out, G0_out[3]);
  or P5 (P5_out, xor_1_out[5], A[5]);
  and G5 (G0_out[5], xor_1_out[5], A[5]);
  and and_21 (and_21_out, P5_out, G0_out[4]);
  and and_22 (and_22_out, Op, P0_out, P1_out, P2_out, P3_out, P4_out);
  or or_5 (or_5_out, and_22_out, and_24_out, and_23_out, and_25_out, and_26_out, G0_out[4]);
  main_2 main_2_3 (.S(S[5]), .A(A[5]), .B(xor_1_out[5]), .Cin(or_5_out));
  and and_23 (and_23_out, P4_out, P3_out, P2_out, G0_out[1]);
  and and_24 (and_24_out, P4_out, P3_out, P2_out, P1_out, G0_out[0]);
  and and_25 (and_25_out, P4_out, P3_out, G0_out[2]);
  or P4 (P4_out, xor_1_out[4], A[4]);
  and G4 (G0_out[4], xor_1_out[4], A[4]);
  and and_26 (and_26_out, P4_out, G0_out[3]);
  and and_27 (and_27_out, Op, P0_out, P1_out, P2_out, P3_out);
  and and_28 (and_28_out, P3_out, P2_out, P1_out, G0_out[0]);
  or or_6 (or_6_out, and_27_out, and_28_out, and_29_out, and_30_out, G0_out[3]);
  main_2 main_2_4 (.S(S[4]), .A(A[4]), .B(xor_1_out[4]), .Cin(or_6_out));
  or P3 (P3_out, xor_1_out[3], A[3]);
  and G3 (G0_out[3], xor_1_out[3], A[3]);
  and and_29 (and_29_out, P3_out, P2_out, G0_out[1]);
  and and_30 (and_30_out, P3_out, G0_out[2]);
  and and_31 (and_31_out, P2_out, P1_out, G0_out[0]);
  and and_32 (and_32_out, Op, P0_out, P1_out, P2_out);
  or or_7 (or_7_out, and_32_out, and_31_out, and_33_out, G0_out[2]);
  main_2 main_2_5 (.S(S[3]), .A(A[3]), .B(xor_1_out[3]), .Cin(or_7_out));
  or P2 (P2_out, xor_1_out[2], A[2]);
  and G2 (G0_out[2], xor_1_out[2], A[2]);
  and and_33 (and_33_out, P2_out, G0_out[1]);
  and and_34 (and_34_out, P0_out, P1_out, Op);
  or or_8 (or_8_out, and_34_out, and_35_out, G0_out[1]);
  main_2 main_2_6 (.S(S[2]), .A(A[2]), .B(xor_1_out[2]), .Cin(or_8_out));
  or P1 (P1_out, xor_1_out[1], A[1]);
  and G1 (G0_out[1], xor_1_out[1], A[1]);
  and and_35 (and_35_out, P1_out, G0_out[0]);
  or P0 (P0_out, xor_1_out[0], A[0]);
  and G0 (G0_out[0], xor_1_out[0], A[0]);
  and and_36 (and_36_out, P0_out, Op);
  or or_9 (or_9_out, and_36_out, G0_out[0]);
  main_2 main_2_7 (.S(S[1]), .A(A[1]), .B(xor_1_out[1]), .Cin(or_9_out));
  main_2 main_2_8 (.S(S[0]), .A(A[0]), .B(xor_1_out[0]), .Cin(Op));

  assign S[7] = Bit;
endmodule

module main_2 (
  input  A,
  input  B,
  input  Cin,
  output S
);

  wire xor_1_out;

  xor xor_1 (xor_1_out, B, A);
  xor xor_2 (S, xor_1_out, Cin);
endmodule
