// Logisim project multiplicador.circ as structural Verilog: 6 circuits, main circuit main
module main (
  input  [7:0] in_1,
  input  [7:0] in_2,
  output [15:0] out_3
);

  wire _1_2, _1_3, _1_4, _1_5, _1_6, _1_7, _1_8, _2_1, _2_2, _2_3, _2_4, _2_5, _2_6, _2_7, _2_8, _3_1, _3_2,
       _3_3, _3_4, _3_5, _3_6, _3_7, _3_8, _4_1, _4_2, _4_3, _4_4, _4_5, _4_6, _4_7, _4_8, _5_1, _5_2, _5_3,
       _5_4, _5_5, _5_6, _5_7, _5_8, _6_1, _6_2, _6_3, _6_4, _6_5, _6_6, _6_7, _6_8, _7_1, _7_2, _7_3, _7_4,
       _7_5, _7_6, _7_7, _7_8, _8_1, _8_2, _8_3, _8_4, _8_5, _8_6, _8_7, _8_8, somador8_1_cout, somador8_1_s,
       somador8_2_cout, somador8_3_cout, somador8_4_cout, somador8_5_cout, somador8_6_cout, somador8_7_cout,
       somador8_8_cout, somadorcompleto8_2_cout, somadorcompleto8_2_s, somadorcompleto8_3_cout,
       somadorcompleto8_3_s, somadorcompleto8_4_cout, somadorcompleto8_4_s, somadorcompleto8_5_cout,
       somadorcompleto8_6_cout, somadorcompleto8_7_cout, somadorcompleto8_7_s, somadorcompleto8_8_cout,
       somadorcompleto8_8_s, somadorcompleto8_9_cout, somadorcompleto8_9_s, somadorcompleto8_10_cout,
       somadorcompleto8_11_cout, somadorcompleto8_11_s, somadorcompleto8_12_cout, somadorcompleto8_12_s,
       somadorcompleto8_13_cout, somadorcompleto8_13_s, somadorcompleto8_14_cout, somadorcompleto8_14_s,
       somadorcompleto8_15_cout, somadorcompleto8_15_s, somadorcompleto8_16_cout, somadorcompleto8_16_s,
       somadorcompleto8_17_cout, somadorcompleto8_17_s, somadorcompleto8_18_cout, somadorcompleto8_18_s,
       somadorcompleto8_19_cout, somadorcompleto8_19_s, somadorcompleto8_20_cout, somadorcompleto8_21_cout,
       somadorcompleto8_22_cout, somadorcompleto8_22_s, somadorcompleto8_23_cout, somadorcompleto8_23_s,
       somadorcompleto8_24_cout, somadorcompleto8_24_s, somadorcompleto8_25_cout, somadorcompleto8_25_s,
       somadorcompleto8_26_cout, somadorcompleto8_26_s, somadorcompleto8_27_cout, somadorcompleto8_27_s,
       somadorcompleto8_28_cout, somadorcompleto8_28_s, somadorcompleto8_29_cout, somadorcompleto8_29_s,
       somadorcompleto8_30_cout, somadorcompleto8_30_s, somadorcompleto8_31_cout, somadorcompleto8_31_s,
       somadorcompleto8_32_cout, somadorcompleto8_32_s, somadorcompleto8_33_cout, somadorcompleto8_34_cout,
       somadorcompleto8_34_s, somadorcompleto8_35_cout, somadorcompleto8_35_s, somadorcompleto8_36_cout,
       somadorcompleto8_36_s, somadorcompleto8_37_cout, somadorcompleto8_37_s, somadorcompleto8_38_cout,
       somadorcompleto8_38_s, somadorcompleto8_39_cout, somadorcompleto8_39_s, somadorcompleto8_40_cout,
       somadorcompleto8_40_s, somadorcompleto8_41_cout, somadorcompleto8_41_s, somadorcompleto8_42_cout,
       somadorcompleto8_42_s, somadorcompleto8_43_cout, somadorcompleto8_43_s, somadorcompleto8_44_cout,
       somadorcompleto8_44_s, somadorcompleto8_45_cout, somadorcompleto8_45_s, somadorcompleto8_46_cout,
       somadorcompleto8_46_s, somadorcompleto8_47_cout, somadorcompleto8_47_s, somadorcompleto8_48_cout,
       somadorcompleto8_48_s;

  somadorcompleto8 somadorcompleto8_1 (
    .Cout(out_3[15]), .S(out_3[14]), .A(somadorcompleto8_3_cout), .B(_8_8), .C(somadorcompleto8_6_cout));
  somadorcompleto8 somadorcompleto8_2 (
    .Cout(somadorcompleto8_2_cout), .S(somadorcompleto8_2_s), .A(somadorcompleto8_7_cout), .B(_8_6),
    .C(somadorcompleto8_8_cout));
  somadorcompleto8 somadorcompleto8_3 (
    .Cout(somadorcompleto8_3_cout), .S(somadorcompleto8_3_s), .A(somadorcompleto8_2_cout), .B(_8_7),
    .C(somadorcompleto8_4_cout));
  somadorcompleto8 somadorcompleto8_4 (
    .Cout(somadorcompleto8_4_cout), .S(somadorcompleto8_4_s), .A(somadorcompleto8_2_s), .B(_7_7),
    .C(somadorcompleto8_9_cout));
  somadorcompleto8 somadorcompleto8_5 (
    .Cout(somadorcompleto8_5_cout), .S(out_3[12]), .A(somadorcompleto8_4_s), .B(_6_8),
    .C(somadorcompleto8_10_cout));
  somadorcompleto8 somadorcompleto8_6 (
    .Cout(somadorcompleto8_6_cout), .S(out_3[13]), .A(somadorcompleto8_3_s), .B(_7_8),
    .C(somadorcompleto8_5_cout));
  somadorcompleto8 somadorcompleto8_7 (
    .Cout(somadorcompleto8_7_cout), .S(somadorcompleto8_7_s), .A(somadorcompleto8_12_cout), .B(_8_5),
    .C(somadorcompleto8_15_cout));
  somadorcompleto8 somadorcompleto8_8 (
    .Cout(somadorcompleto8_8_cout), .S(somadorcompleto8_8_s), .A(somadorcompleto8_7_s), .B(_7_6),
    .C(somadorcompleto8_17_cout));
  somadorcompleto8 somadorcompleto8_9 (
    .Cout(somadorcompleto8_9_cout), .S(somadorcompleto8_9_s), .A(somadorcompleto8_8_s), .B(_6_7),
    .C(somadorcompleto8_18_cout));
  somadorcompleto8 somadorcompleto8_10 (
    .Cout(somadorcompleto8_10_cout), .S(out_3[11]), .A(somadorcompleto8_9_s), .B(_5_8),
    .C(somadorcompleto8_20_cout));
  somador8 somador8_1 (.A(_8_2), .B(somadorcompleto8_22_cout), .S(somador8_1_s), .Cout(somador8_1_cout));
  somadorcompleto8 somadorcompleto8_11 (
    .Cout(somadorcompleto8_11_cout), .S(somadorcompleto8_11_s), .A(somador8_1_cout), .B(_8_3),
    .C(somadorcompleto8_24_cout));
  somadorcompleto8 somadorcompleto8_12 (
    .Cout(somadorcompleto8_12_cout), .S(somadorcompleto8_12_s), .A(somadorcompleto8_11_cout), .B(_8_4),
    .C(somadorcompleto8_13_cout));
  somadorcompleto8 somadorcompleto8_13 (
    .Cout(somadorcompleto8_13_cout), .S(somadorcompleto8_13_s), .A(somadorcompleto8_11_s), .B(_7_4),
    .C(somadorcompleto8_25_cout));
  somadorcompleto8 somadorcompleto8_14 (
    .Cout(somadorcompleto8_14_cout), .S(somadorcompleto8_14_s), .A(somadorcompleto8_13_s), .B(_6_5),
    .C(somadorcompleto8_28_cout));
  somadorcompleto8 somadorcompleto8_15 (
    .Cout(somadorcompleto8_15_cout), .S(somadorcompleto8_15_s), .A(somadorcompleto8_12_s), .B(_7_5),
    .C(somadorcompleto8_14_cout));
  somadorcompleto8 somadorcompleto8_16 (
    .Cout(somadorcompleto8_16_cout), .S(somadorcompleto8_16_s), .A(somadorcompleto8_14_s), .B(_5_6),
    .C(somadorcompleto8_29_cout));
  somadorcompleto8 somadorcompleto8_17 (
    .Cout(somadorcompleto8_17_cout), .S(somadorcompleto8_17_s), .A(somadorcompleto8_15_s), .B(_6_6),
    .C(somadorcompleto8_16_cout));
  somadorcompleto8 somadorcompleto8_18 (
    .Cout(somadorcompleto8_18_cout), .S(somadorcompleto8_18_s), .A(somadorcompleto8_17_s), .B(_5_7),
    .C(somadorcompleto8_19_cout));
  somadorcompleto8 somadorcompleto8_19 (
    .Cout(somadorcompleto8_19_cout), .S(somadorcompleto8_19_s), .A(somadorcompleto8_16_s), .B(_4_7),
    .C(somadorcompleto8_32_cout));
  somadorcompleto8 somadorcompleto8_20 (
    .Cout(somadorcompleto8_20_cout), .S(out_3[10]), .A(somadorcompleto8_18_s), .B(_4_8),
    .C(somadorcompleto8_21_cout));
  somadorcompleto8 somadorcompleto8_21 (
    .Cout(somadorcompleto8_21_cout), .S(out_3[9]), .A(somadorcompleto8_19_s), .B(_3_8),
    .C(somadorcompleto8_33_cout));
  somadorcompleto8 somadorcompleto8_22 (
    .Cout(somadorcompleto8_22_cout), .S(somadorcompleto8_22_s), .A(_7_2), .B(_8_1),
    .C(somadorcompleto8_34_cout));
  somadorcompleto8 somadorcompleto8_23 (
    .Cout(somadorcompleto8_23_cout), .S(somadorcompleto8_23_s), .A(somadorcompleto8_22_s), .B(_6_3),
    .C(somadorcompleto8_35_cout));
  somadorcompleto8 somadorcompleto8_24 (
    .Cout(somadorcompleto8_24_cout), .S(somadorcompleto8_24_s), .A(somador8_1_s), .B(_7_3),
    .C(somadorcompleto8_23_cout));
  somadorcompleto8 somadorcompleto8_25 (
    .Cout(somadorcompleto8_25_cout), .S(somadorcompleto8_25_s), .A(somadorcompleto8_24_s), .B(_6_4),
    .C(somadorcompleto8_26_cout));
  somadorcompleto8 somadorcompleto8_26 (
    .Cout(somadorcompleto8_26_cout), .S(somadorcompleto8_26_s), .A(somadorcompleto8_23_s), .B(_5_4),
    .C(somadorcompleto8_36_cout));
  somadorcompleto8 somadorcompleto8_27 (
    .Cout(somadorcompleto8_27_cout), .S(somadorcompleto8_27_s), .A(somadorcompleto8_26_s), .B(_4_5),
    .C(somadorcompleto8_37_cout));
  somadorcompleto8 somadorcompleto8_28 (
    .Cout(somadorcompleto8_28_cout), .S(somadorcompleto8_28_s), .A(somadorcompleto8_25_s), .B(_5_5),
    .C(somadorcompleto8_27_cout));
  somadorcompleto8 somadorcompleto8_29 (
    .Cout(somadorcompleto8_29_cout), .S(somadorcompleto8_29_s), .A(somadorcompleto8_28_s), .B(_4_6),
    .C(somadorcompleto8_30_cout));
  somadorcompleto8 somadorcompleto8_30 (
    .Cout(somadorcompleto8_30_cout), .S(somadorcompleto8_30_s), .A(somadorcompleto8_27_s), .B(_3_6),
    .C(somadorcompleto8_38_cout));
  somadorcompleto8 somadorcompleto8_31 (
    .Cout(somadorcompleto8_31_cout), .S(somadorcompleto8_31_s), .A(somadorcompleto8_30_s), .B(_2_7),
    .C(somador8_4_cout));
  somadorcompleto8 somadorcompleto8_32 (
    .Cout(somadorcompleto8_32_cout), .S(somadorcompleto8_32_s), .A(somadorcompleto8_29_s), .B(_3_7),
    .C(somadorcompleto8_31_cout));
  somador8 somador8_2 (.A(somadorcompleto8_31_s), .B(_1_8), .S(out_3[7]), .Cout(somador8_2_cout));
  somadorcompleto8 somadorcompleto8_33 (
    .Cout(somadorcompleto8_33_cout), .S(out_3[8]), .A(somadorcompleto8_32_s), .B(_2_8), .C(somador8_2_cout));
  somadorcompleto8 somadorcompleto8_34 (
    .Cout(somadorcompleto8_34_cout), .S(somadorcompleto8_34_s), .A(_6_2), .B(_7_1),
    .C(somadorcompleto8_40_cout));
  somadorcompleto8 somadorcompleto8_35 (
    .Cout(somadorcompleto8_35_cout), .S(somadorcompleto8_35_s), .A(somadorcompleto8_34_s), .B(_5_3),
    .C(somadorcompleto8_42_cout));
  somadorcompleto8 somadorcompleto8_36 (
    .Cout(somadorcompleto8_36_cout), .S(somadorcompleto8_36_s), .A(somadorcompleto8_35_s), .B(_4_4),
    .C(somadorcompleto8_44_cout));
  somadorcompleto8 somadorcompleto8_37 (
    .Cout(somadorcompleto8_37_cout), .S(somadorcompleto8_37_s), .A(somadorcompleto8_36_s), .B(_3_5),
    .C(somadorcompleto8_45_cout));
  somadorcompleto8 somadorcompleto8_38 (
    .Cout(somadorcompleto8_38_cout), .S(somadorcompleto8_38_s), .A(somadorcompleto8_37_s), .B(_2_6),
    .C(somador8_3_cout));
  somador8 somador8_3 (.A(somadorcompleto8_45_s), .B(_1_6), .S(out_3[5]), .Cout(somador8_3_cout));
  somador8 somador8_4 (.A(somadorcompleto8_38_s), .B(_1_7), .S(out_3[6]), .Cout(somador8_4_cout));
  somadorcompleto8 somadorcompleto8_39 (
    .Cout(somadorcompleto8_39_cout), .S(somadorcompleto8_39_s), .A(_4_2), .B(_5_1),
    .C(somadorcompleto8_46_cout));
  somadorcompleto8 somadorcompleto8_40 (
    .Cout(somadorcompleto8_40_cout), .S(somadorcompleto8_40_s), .A(_5_2), .B(_6_1),
    .C(somadorcompleto8_39_cout));
  somadorcompleto8 somadorcompleto8_41 (
    .Cout(somadorcompleto8_41_cout), .S(somadorcompleto8_41_s), .A(somadorcompleto8_39_s), .B(_3_3),
    .C(somadorcompleto8_47_cout));
  somadorcompleto8 somadorcompleto8_42 (
    .Cout(somadorcompleto8_42_cout), .S(somadorcompleto8_42_s), .A(somadorcompleto8_40_s), .B(_4_3),
    .C(somadorcompleto8_41_cout));
  somador8 somador8_5 (.A(somadorcompleto8_47_s), .B(_1_4), .S(out_3[3]), .Cout(somador8_5_cout));
  somadorcompleto8 somadorcompleto8_43 (
    .Cout(somadorcompleto8_43_cout), .S(somadorcompleto8_43_s), .A(somadorcompleto8_41_s), .B(_2_4),
    .C(somador8_5_cout));
  somadorcompleto8 somadorcompleto8_44 (
    .Cout(somadorcompleto8_44_cout), .S(somadorcompleto8_44_s), .A(somadorcompleto8_42_s), .B(_3_4),
    .C(somadorcompleto8_43_cout));
  somador8 somador8_6 (.A(somadorcompleto8_43_s), .B(_1_5), .S(out_3[4]), .Cout(somador8_6_cout));
  somadorcompleto8 somadorcompleto8_45 (
    .Cout(somadorcompleto8_45_cout), .S(somadorcompleto8_45_s), .A(somadorcompleto8_44_s), .B(_2_5),
    .C(somador8_6_cout));
  somadorcompleto8 somadorcompleto8_46 (
    .Cout(somadorcompleto8_46_cout), .S(somadorcompleto8_46_s), .A(_3_2), .B(_4_1),
    .C(somadorcompleto8_48_cout));
  somador8 somador8_7 (.A(somadorcompleto8_48_s), .B(_1_3), .S(out_3[2]), .Cout(somador8_7_cout));
  somadorcompleto8 somadorcompleto8_47 (
    .Cout(somadorcompleto8_47_cout), .S(somadorcompleto8_47_s), .A(somadorcompleto8_46_s), .B(_2_3),
    .C(somador8_7_cout));
  somador8 somador8_8 (.A(_1_2), .B(_2_1), .S(out_3[1]), .Cout(somador8_8_cout));
  somadorcompleto8 somadorcompleto8_48 (
    .Cout(somadorcompleto8_48_cout), .S(somadorcompleto8_48_s), .A(_2_2), .B(_3_1), .C(somador8_8_cout));
  and and_1 (_7_1, in_1[6], in_2[0]);
  and and_2 (_8_1, in_1[7], in_2[0]);
  and and_3 (_6_1, in_1[5], in_2[0]);
  and and_4 (_6_2, in_1[5], in_2[1]);
  and and_5 (_8_2, in_1[7], in_2[1]);
  and and_6 (_7_2, in_1[6], in_2[1]);
  and and_7 (_8_3, in_1[7], in_2[2]);
  and and_8 (_6_3, in_1[5], in_2[2]);
  and and_9 (_7_3, in_1[6], in_2[2]);
  and and_10 (_6_4, in_1[5], in_2[3]);
  and and_11 (_8_4, in_1[7], in_2[3]);
  and and_12 (_7_4, in_1[6], in_2[3]);
  and and_13 (_7_5, in_1[6], in_2[4]);
  and and_14 (_6_5, in_1[5], in_2[4]);
  and and_15 (_8_5, in_1[7], in_2[4]);
  and and_16 (_7_6, in_1[6], in_2[5]);
  and and_17 (_6_6, in_1[5], in_2[5]);
  and and_18 (_8_6, in_1[7], in_2[5]);
  and and_19 (_7_7, in_1[6], in_2[6]);
  and and_20 (_6_7, in_1[5], in_2[6]);
  and and_21 (_8_7, in_1[7], in_2[6]);
  and and_22 (_8_8, in_1[7], in_2[7]);
  and and_23 (_6_8, in_1[5], in_2[7]);
  and and_24 (_7_8, in_1[6], in_2[7]);
  and and_25 (_4_1, in_1[3], in_2[0]);
  and and_26 (_5_1, in_1[4], in_2[0]);
  and and_27 (_4_2, in_1[3], in_2[1]);
  and and_28 (_5_2, in_1[4], in_2[1]);
  and and_29 (_5_3, in_1[4], in_2[2]);
  and and_30 (_4_3, in_1[3], in_2[2]);
  and and_31 (_4_4, in_1[3], in_2[3]);
  and and_32 (_5_4, in_1[4], in_2[3]);
  and and_33 (_5_5, in_1[4], in_2[4]);
  and and_34 (_4_5, in_1[3], in_2[4]);
  and and_35 (_5_6, in_1[4], in_2[5]);
  and and_36 (_4_6, in_1[3], in_2[5]);
  and and_37 (_5_7, in_1[4], in_2[6]);
  and and_38 (_4_7, in_1[3], in_2[6]);
  and and_39 (_5_8, in_1[4], in_2[7]);
  and and_40 (_4_8, in_1[3], in_2[7]);
  and and_41 (_3_1, in_1[2], in_2[0]);
  and and_42 (_2_1, in_1[1], in_2[0]);
  and and_43 (out_3[0], in_1[0], in_2[0]);
  and and_44 (_2_2, in_1[1], in_2[1]);
  and and_45 (_1_2, in_1[0], in_2[1]);
  and and_46 (_3_2, in_1[2], in_2[1]);
  and and_47 (_1_3, in_1[0], in_2[2]);
  and and_48 (_3_3, in_1[2], in_2[2]);
  and and_49 (_2_3, in_1[1], in_2[2]);
  and and_50 (_2_4, in_1[1], in_2[3]);
  and and_51 (_1_4, in_1[0], in_2[3]);
  and and_52 (_3_4, in_1[2], in_2[3]);
  and and_53 (_1_5, in_1[0], in_2[4]);
  and and_54 (_2_5, in_1[1], in_2[4]);
  and and_55 (_3_5, in_1[2], in_2[4]);
  and and_56 (_3_6, in_1[2], in_2[5]);
  and and_57 (_2_6, in_1[1], in_2[5]);
  and and_58 (_1_6, in_1[0], in_2[5]);
  and and_59 (_2_7, in_1[1], in_2[6]);
  and and_60 (_1_7, in_1[0], in_2[6]);
  and and_61 (_3_7, in_1[2], in_2[6]);
  and and_62 (_2_8, in_1[1], in_2[7]);
  and and_63 (_1_8, in_1[0], in_2[7]);
  and and_64 (_3_8, in_1[2], in_2[7]);

  // Other names for the same wires on the sheet: _1_1 = out_3[0]
endmodule

module somador (
  input  A,
  input  B,
  output S,
  output Cout
);

  xor xor_1 (S, A, B);
  and and_1 (Cout, A, B);
endmodule

module somadorCompleto (
  input  A,
  input  B,
  input  C,
  output Cout,
  output S
);

  wire and_1_out, and_2_out, and_3_out, xor_1_out;

  and and_1 (and_1_out, A, B);
  and and_2 (and_2_out, B, C);
  and and_3 (and_3_out, C, A);
  xor xor_1 (xor_1_out, A, B);
  xor xor_2 (S, xor_1_out, C);
  or or_1 (Cout, and_1_out, and_2_out, and_3_out);
endmodule

module main8bits (
  input  [7:0] in_1,
  input  [7:0] in_2,
  output [15:0] out_3
);

  wire _1_2, _1_3, _1_4, _1_5, _1_6, _1_7, _1_8, _2_1, _2_2, _2_3, _2_4, _2_5, _2_6, _2_7, _2_8, _3_1, _3_2,
       _3_3, _3_4, _3_5, _3_6, _3_7, _3_8, _4_1, _4_2, _4_3, _4_4, _4_5, _4_6, _4_7, _4_8, _5_1, _5_2, _5_3,
       _5_4, _5_5, _5_6, _5_7, _5_8, _6_1, _6_2, _6_3, _6_4, _6_5, _6_6, _6_7, _6_8, _7_1, _7_2, _7_3, _7_4,
       _7_5, _7_6, _7_7, _7_8, _8_1, _8_2, _8_3, _8_4, _8_5, _8_6, _8_7, _8_8, somador8_1_cout, somador8_1_s,
       somador8_2_cout, somador8_3_cout, somador8_4_cout, somador8_5_cout, somador8_6_cout, somador8_7_cout,
       somador8_8_cout, somadorcompleto8_2_cout, somadorcompleto8_2_s, somadorcompleto8_3_cout,
       somadorcompleto8_3_s, somadorcompleto8_4_cout, somadorcompleto8_4_s, somadorcompleto8_5_cout,
       somadorcompleto8_6_cout, somadorcompleto8_7_cout, somadorcompleto8_7_s, somadorcompleto8_8_cout,
       somadorcompleto8_8_s, somadorcompleto8_9_cout, somadorcompleto8_9_s, somadorcompleto8_10_cout,
       somadorcompleto8_11_cout, somadorcompleto8_11_s, somadorcompleto8_12_cout, somadorcompleto8_12_s,
       somadorcompleto8_13_cout, somadorcompleto8_13_s, somadorcompleto8_14_cout, somadorcompleto8_14_s,
       somadorcompleto8_15_cout, somadorcompleto8_15_s, somadorcompleto8_16_cout, somadorcompleto8_16_s,
       somadorcompleto8_17_cout, somadorcompleto8_17_s, somadorcompleto8_18_cout, somadorcompleto8_18_s,
       somadorcompleto8_19_cout, somadorcompleto8_19_s, somadorcompleto8_20_cout, somadorcompleto8_21_cout,
       somadorcompleto8_22_cout, somadorcompleto8_22_s, somadorcompleto8_23_cout, somadorcompleto8_23_s,
       somadorcompleto8_24_cout, somadorcompleto8_24_s, somadorcompleto8_25_cout, somadorcompleto8_25_s,
       somadorcompleto8_26_cout, somadorcompleto8_26_s, somadorcompleto8_27_cout, somadorcompleto8_27_s,
       somadorcompleto8_28_cout, somadorcompleto8_28_s, somadorcompleto8_29_cout, somadorcompleto8_29_s,
       somadorcompleto8_30_cout, somadorcompleto8_30_s, somadorcompleto8_31_cout, somadorcompleto8_31_s,
       somadorcompleto8_32_cout, somadorcompleto8_32_s, somadorcompleto8_33_cout, somadorcompleto8_34_cout,
       somadorcompleto8_34_s, somadorcompleto8_35_cout, somadorcompleto8_35_s, somadorcompleto8_36_cout,
       somadorcompleto8_36_s, somadorcompleto8_37_cout, somadorcompleto8_37_s, somadorcompleto8_38_cout,
       somadorcompleto8_38_s, somadorcompleto8_39_cout, somadorcompleto8_39_s, somadorcompleto8_40_cout,
       somadorcompleto8_40_s, somadorcompleto8_41_cout, somadorcompleto8_41_s, somadorcompleto8_42_cout,
       somadorcompleto8_42_s, somadorcompleto8_43_cout, somadorcompleto8_43_s, somadorcompleto8_44_cout,
       somadorcompleto8_44_s, somadorcompleto8_45_cout, somadorcompleto8_45_s, somadorcompleto8_46_cout,
       somadorcompleto8_46_s, somadorcompleto8_47_cout, somadorcompleto8_47_s, somadorcompleto8_48_cout,
       somadorcompleto8_48_s;

  somadorcompleto8 somadorcompleto8_1 (
    .Cout(out_3[15]), .S(out_3[14]), .A(somadorcompleto8_3_cout), .B(_8_8), .C(somadorcompleto8_5_cout));
  somadorcompleto8 somadorcompleto8_2 (
    .Cout(somadorcompleto8_2_cout), .S(somadorcompleto8_2_s), .A(somadorcompleto8_7_cout), .B(_8_6),
    .C(somadorcompleto8_8_cout));
  somadorcompleto8 somadorcompleto8_3 (
    .Cout(somadorcompleto8_3_cout), .S(somadorcompleto8_3_s), .A(somadorcompleto8_2_cout), .B(_8_7),
    .C(somadorcompleto8_4_cout));
  somadorcompleto8 somadorcompleto8_4 (
    .Cout(somadorcompleto8_4_cout), .S(somadorcompleto8_4_s), .A(somadorcompleto8_2_s), .B(_7_7),
    .C(somadorcompleto8_9_cout));
  somadorcompleto8 somadorcompleto8_5 (
    .Cout(somadorcompleto8_5_cout), .S(out_3[13]), .A(somadorcompleto8_3_s), .B(_7_8),
    .C(somadorcompleto8_6_cout));
  somadorcompleto8 somadorcompleto8_6 (
    .Cout(somadorcompleto8_6_cout), .S(out_3[12]), .A(somadorcompleto8_4_s), .B(_6_8),
    .C(somadorcompleto8_10_cout));
  somadorcompleto8 somadorcompleto8_7 (
    .Cout(somadorcompleto8_7_cout), .S(somadorcompleto8_7_s), .A(somadorcompleto8_13_cout), .B(_8_5),
    .C(somadorcompleto8_14_cout));
  somadorcompleto8 somadorcompleto8_8 (
    .Cout(somadorcompleto8_8_cout), .S(somadorcompleto8_8_s), .A(somadorcompleto8_7_s), .B(_7_6),
    .C(somadorcompleto8_16_cout));
  somadorcompleto8 somadorcompleto8_9 (
    .Cout(somadorcompleto8_9_cout), .S(somadorcompleto8_9_s), .A(somadorcompleto8_8_s), .B(_6_7),
    .C(somadorcompleto8_18_cout));
  somadorcompleto8 somadorcompleto8_10 (
    .Cout(somadorcompleto8_10_cout), .S(out_3[11]), .A(somadorcompleto8_9_s), .B(_5_8),
    .C(somadorcompleto8_20_cout));
  somador8 somador8_1 (.A(_8_2), .B(somadorcompleto8_22_cout), .S(somador8_1_s), .Cout(somador8_1_cout));
  somadorcompleto8 somadorcompleto8_11 (
    .Cout(somadorcompleto8_11_cout), .S(somadorcompleto8_11_s), .A(somador8_1_cout), .B(_8_3),
    .C(somadorcompleto8_23_cout));
  somadorcompleto8 somadorcompleto8_12 (
    .Cout(somadorcompleto8_12_cout), .S(somadorcompleto8_12_s), .A(somadorcompleto8_11_s), .B(_7_4),
    .C(somadorcompleto8_25_cout));
  somadorcompleto8 somadorcompleto8_13 (
    .Cout(somadorcompleto8_13_cout), .S(somadorcompleto8_13_s), .A(somadorcompleto8_11_cout), .B(_8_4),
    .C(somadorcompleto8_12_cout));
  somadorcompleto8 somadorcompleto8_14 (
    .Cout(somadorcompleto8_14_cout), .S(somadorcompleto8_14_s), .A(somadorcompleto8_13_s), .B(_7_5),
    .C(somadorcompleto8_15_cout));
  somadorcompleto8 somadorcompleto8_15 (
    .Cout(somadorcompleto8_15_cout), .S(somadorcompleto8_15_s), .A(somadorcompleto8_12_s), .B(_6_5),
    .C(somadorcompleto8_27_cout));
  somadorcompleto8 somadorcompleto8_16 (
    .Cout(somadorcompleto8_16_cout), .S(somadorcompleto8_16_s), .A(somadorcompleto8_14_s), .B(_6_6),
    .C(somadorcompleto8_17_cout));
  somadorcompleto8 somadorcompleto8_17 (
    .Cout(somadorcompleto8_17_cout), .S(somadorcompleto8_17_s), .A(somadorcompleto8_15_s), .B(_5_6),
    .C(somadorcompleto8_30_cout));
  somadorcompleto8 somadorcompleto8_18 (
    .Cout(somadorcompleto8_18_cout), .S(somadorcompleto8_18_s), .A(somadorcompleto8_16_s), .B(_5_7),
    .C(somadorcompleto8_19_cout));
  somadorcompleto8 somadorcompleto8_19 (
    .Cout(somadorcompleto8_19_cout), .S(somadorcompleto8_19_s), .A(somadorcompleto8_17_s), .B(_4_7),
    .C(somadorcompleto8_32_cout));
  somadorcompleto8 somadorcompleto8_20 (
    .Cout(somadorcompleto8_20_cout), .S(out_3[10]), .A(somadorcompleto8_18_s), .B(_4_8),
    .C(somadorcompleto8_21_cout));
  somadorcompleto8 somadorcompleto8_21 (
    .Cout(somadorcompleto8_21_cout), .S(out_3[9]), .A(somadorcompleto8_19_s), .B(_3_8),
    .C(somadorcompleto8_33_cout));
  somadorcompleto8 somadorcompleto8_22 (
    .Cout(somadorcompleto8_22_cout), .S(somadorcompleto8_22_s), .A(_7_2), .B(_8_1),
    .C(somadorcompleto8_34_cout));
  somadorcompleto8 somadorcompleto8_23 (
    .Cout(somadorcompleto8_23_cout), .S(somadorcompleto8_23_s), .A(somador8_1_s), .B(_7_3),
    .C(somadorcompleto8_24_cout));
  somadorcompleto8 somadorcompleto8_24 (
    .Cout(somadorcompleto8_24_cout), .S(somadorcompleto8_24_s), .A(somadorcompleto8_22_s), .B(_6_3),
    .C(somadorcompleto8_35_cout));
  somadorcompleto8 somadorcompleto8_25 (
    .Cout(somadorcompleto8_25_cout), .S(somadorcompleto8_25_s), .A(somadorcompleto8_23_s), .B(_6_4),
    .C(somadorcompleto8_26_cout));
  somadorcompleto8 somadorcompleto8_26 (
    .Cout(somadorcompleto8_26_cout), .S(somadorcompleto8_26_s), .A(somadorcompleto8_24_s), .B(_5_4),
    .C(somadorcompleto8_36_cout));
  somadorcompleto8 somadorcompleto8_27 (
    .Cout(somadorcompleto8_27_cout), .S(somadorcompleto8_27_s), .A(somadorcompleto8_25_s), .B(_5_5),
    .C(somadorcompleto8_28_cout));
  somadorcompleto8 somadorcompleto8_28 (
    .Cout(somadorcompleto8_28_cout), .S(somadorcompleto8_28_s), .A(somadorcompleto8_26_s), .B(_4_5),
    .C(somadorcompleto8_37_cout));
  somadorcompleto8 somadorcompleto8_29 (
    .Cout(somadorcompleto8_29_cout), .S(somadorcompleto8_29_s), .A(somadorcompleto8_28_s), .B(_3_6),
    .C(somadorcompleto8_38_cout));
  somadorcompleto8 somadorcompleto8_30 (
    .Cout(somadorcompleto8_30_cout), .S(somadorcompleto8_30_s), .A(somadorcompleto8_27_s), .B(_4_6),
    .C(somadorcompleto8_29_cout));
  somadorcompleto8 somadorcompleto8_31 (
    .Cout(somadorcompleto8_31_cout), .S(somadorcompleto8_31_s), .A(somadorcompleto8_29_s), .B(_2_7),
    .C(somador8_4_cout));
  somadorcompleto8 somadorcompleto8_32 (
    .Cout(somadorcompleto8_32_cout), .S(somadorcompleto8_32_s), .A(somadorcompleto8_30_s), .B(_3_7),
    .C(somadorcompleto8_31_cout));
  somadorcompleto8 somadorcompleto8_33 (
    .Cout(somadorcompleto8_33_cout), .S(out_3[8]), .A(somadorcompleto8_32_s), .B(_2_8), .C(somador8_2_cout));
  somador8 somador8_2 (.A(somadorcompleto8_31_s), .B(_1_8), .S(out_3[7]), .Cout(somador8_2_cout));
  somadorcompleto8 somadorcompleto8_34 (
    .Cout(somadorcompleto8_34_cout), .S(somadorcompleto8_34_s), .A(_6_2), .B(_7_1),
    .C(somadorcompleto8_39_cout));
  somadorcompleto8 somadorcompleto8_35 (
    .Cout(somadorcompleto8_35_cout), .S(somadorcompleto8_35_s), .A(somadorcompleto8_34_s), .B(_5_3),
    .C(somadorcompleto8_42_cout));
  somadorcompleto8 somadorcompleto8_36 (
    .Cout(somadorcompleto8_36_cout), .S(somadorcompleto8_36_s), .A(somadorcompleto8_35_s), .B(_4_4),
    .C(somadorcompleto8_44_cout));
  somadorcompleto8 somadorcompleto8_37 (
    .Cout(somadorcompleto8_37_cout), .S(somadorcompleto8_37_s), .A(somadorcompleto8_36_s), .B(_3_5),
    .C(somadorcompleto8_45_cout));
  somadorcompleto8 somadorcompleto8_38 (
    .Cout(somadorcompleto8_38_cout), .S(somadorcompleto8_38_s), .A(somadorcompleto8_37_s), .B(_2_6),
    .C(somador8_3_cout));
  somador8 somador8_3 (.A(somadorcompleto8_45_s), .B(_1_6), .S(out_3[5]), .Cout(somador8_3_cout));
  somador8 somador8_4 (.A(somadorcompleto8_38_s), .B(_1_7), .S(out_3[6]), .Cout(somador8_4_cout));
  somadorcompleto8 somadorcompleto8_39 (
    .Cout(somadorcompleto8_39_cout), .S(somadorcompleto8_39_s), .A(_5_2), .B(_6_1),
    .C(somadorcompleto8_40_cout));
  somadorcompleto8 somadorcompleto8_40 (
    .Cout(somadorcompleto8_40_cout), .S(somadorcompleto8_40_s), .A(_4_2), .B(_5_1),
    .C(somadorcompleto8_46_cout));
  somadorcompleto8 somadorcompleto8_41 (
    .Cout(somadorcompleto8_41_cout), .S(somadorcompleto8_41_s), .A(somadorcompleto8_40_s), .B(_3_3),
    .C(somadorcompleto8_47_cout));
  somadorcompleto8 somadorcompleto8_42 (
    .Cout(somadorcompleto8_42_cout), .S(somadorcompleto8_42_s), .A(somadorcompleto8_39_s), .B(_4_3),
    .C(somadorcompleto8_41_cout));
  somador8 somador8_5 (.A(somadorcompleto8_47_s), .B(_1_4), .S(out_3[3]), .Cout(somador8_5_cout));
  somadorcompleto8 somadorcompleto8_43 (
    .Cout(somadorcompleto8_43_cout), .S(somadorcompleto8_43_s), .A(somadorcompleto8_41_s), .B(_2_4),
    .C(somador8_5_cout));
  somadorcompleto8 somadorcompleto8_44 (
    .Cout(somadorcompleto8_44_cout), .S(somadorcompleto8_44_s), .A(somadorcompleto8_42_s), .B(_3_4),
    .C(somadorcompleto8_43_cout));
  somador8 somador8_6 (.A(somadorcompleto8_43_s), .B(_1_5), .S(out_3[4]), .Cout(somador8_6_cout));
  somadorcompleto8 somadorcompleto8_45 (
    .Cout(somadorcompleto8_45_cout), .S(somadorcompleto8_45_s), .A(somadorcompleto8_44_s), .B(_2_5),
    .C(somador8_6_cout));
  somadorcompleto8 somadorcompleto8_46 (
    .Cout(somadorcompleto8_46_cout), .S(somadorcompleto8_46_s), .A(_3_2), .B(_4_1),
    .C(somadorcompleto8_48_cout));
  somadorcompleto8 somadorcompleto8_47 (
    .Cout(somadorcompleto8_47_cout), .S(somadorcompleto8_47_s), .A(somadorcompleto8_46_s), .B(_2_3),
    .C(somador8_7_cout));
  somador8 somador8_7 (.A(somadorcompleto8_48_s), .B(_1_3), .S(out_3[2]), .Cout(somador8_7_cout));
  somador8 somador8_8 (.A(_1_2), .B(_2_1), .S(out_3[1]), .Cout(somador8_8_cout));
  somadorcompleto8 somadorcompleto8_48 (
    .Cout(somadorcompleto8_48_cout), .S(somadorcompleto8_48_s), .A(_2_2), .B(_3_1), .C(somador8_8_cout));
  and and_1 (_8_1, in_1[7], in_2[0]);
  and and_2 (_6_1, in_1[5], in_2[0]);
  and and_3 (_7_1, in_1[6], in_2[0]);
  and and_4 (_6_2, in_1[5], in_2[1]);
  and and_5 (_8_2, in_1[7], in_2[1]);
  and and_6 (_7_2, in_1[6], in_2[1]);
  and and_7 (_7_3, in_1[6], in_2[2]);
  and and_8 (_8_3, in_1[7], in_2[2]);
  and and_9 (_6_3, in_1[5], in_2[2]);
  and and_10 (_8_4, in_1[7], in_2[3]);
  and and_11 (_7_4, in_1[6], in_2[3]);
  and and_12 (_6_4, in_1[5], in_2[3]);
  and and_13 (_8_5, in_1[7], in_2[4]);
  and and_14 (_6_5, in_1[5], in_2[4]);
  and and_15 (_7_5, in_1[6], in_2[4]);
  and and_16 (_6_6, in_1[5], in_2[5]);
  and and_17 (_8_6, in_1[7], in_2[5]);
  and and_18 (_7_6, in_1[6], in_2[5]);
  and and_19 (_6_7, in_1[5], in_2[6]);
  and and_20 (_8_7, in_1[7], in_2[6]);
  and and_21 (_7_7, in_1[6], in_2[6]);
  and and_22 (_6_8, in_1[5], in_2[7]);
  and and_23 (_8_8, in_1[7], in_2[7]);
  and and_24 (_7_8, in_1[6], in_2[7]);
  and and_25 (_4_1, in_1[3], in_2[0]);
  and and_26 (_5_1, in_1[4], in_2[0]);
  and and_27 (_5_2, in_1[4], in_2[1]);
  and and_28 (_4_2, in_1[3], in_2[1]);
  and and_29 (_5_3, in_1[4], in_2[2]);
  and and_30 (_4_3, in_1[3], in_2[2]);
  and and_31 (_5_4, in_1[4], in_2[3]);
  and and_32 (_4_4, in_1[3], in_2[3]);
  and and_33 (_5_5, in_1[4], in_2[4]);
  and and_34 (_4_5, in_1[3], in_2[4]);
  and and_35 (_4_6, in_1[3], in_2[5]);
  and and_36 (_5_6, in_1[4], in_2[5]);
  and and_37 (_5_7, in_1[4], in_2[6]);
  and and_38 (_4_7, in_1[3], in_2[6]);
  and and_39 (_5_8, in_1[4], in_2[7]);
  and and_40 (_4_8, in_1[3], in_2[7]);
  and and_41 (_2_1, in_1[1], in_2[0]);
  and and_42 (out_3[0], in_1[0], in_2[0]);
  and and_43 (_3_1, in_1[2], in_2[0]);
  and and_44 (_3_2, in_1[2], in_2[1]);
  and and_45 (_1_2, in_1[0], in_2[1]);
  and and_46 (_2_2, in_1[1], in_2[1]);
  and and_47 (_2_3, in_1[1], in_2[2]);
  and and_48 (_1_3, in_1[0], in_2[2]);
  and and_49 (_3_3, in_1[2], in_2[2]);
  and and_50 (_2_4, in_1[1], in_2[3]);
  and and_51 (_3_4, in_1[2], in_2[3]);
  and and_52 (_1_4, in_1[0], in_2[3]);
  and and_53 (_2_5, in_1[1], in_2[4]);
  and and_54 (_3_5, in_1[2], in_2[4]);
  and and_55 (_1_5, in_1[0], in_2[4]);
  and and_56 (_1_6, in_1[0], in_2[5]);
  and and_57 (_3_6, in_1[2], in_2[5]);
  and and_58 (_2_6, in_1[1], in_2[5]);
  and and_59 (_3_7, in_1[2], in_2[6]);
  and and_60 (_2_7, in_1[1], in_2[6]);
  and and_61 (_1_7, in_1[0], in_2[6]);
  and and_62 (_3_8, in_1[2], in_2[7]);
  and and_63 (_2_8, in_1[1], in_2[7]);
  and and_64 (_1_8, in_1[0], in_2[7]);

  // Other names for the same wires on the sheet: _1_1 = out_3[0]
endmodule

module somador8 (
  input  A,
  input  B,
  output S,
  output Cout
);

  xor xor_1 (S, A, B);
  and and_1 (Cout, A, B);
endmodule

module somadorcompleto8 (
  input  A,
  input  B,
  input  C,
  output Cout,
  output S
);

  wire and_1_out, and_2_out, and_3_out, xor_1_out;

  and and_1 (and_1_out, A, B);
  and and_2 (and_2_out, B, C);
  and and_3 (and_3_out, C, A);
  xor xor_1 (xor_1_out, A, B);
  xor xor_2 (S, xor_1_out, C);
  or or_1 (Cout, and_1_out, and_2_out, and_3_out);
endmodule
